# Fritzing sketch Temp & Hum (saved by Fritzing 0.9.4)
breadboards: 1

parts:
  Part1 = Arduino Uno (Rev3)
  Part2 = Bluetooth HC-05 Macho
  Mod1 = KY-015 Temperature & Humidity Sensor Module [package="Breakout board"]

nets:
  N1: Part1.A0, Mod1.S
  N2: Part1.D8, Part2.TXD
  N3: Part1.D9_PWM, Part2.RXD
  3V3: Part1.3V3, Part2.VCC
  5V: Part1.5V, Mod1.Vin
  GND: Part1.GND, Part2.GND, Mod1.-

custom parts:
  KY-015 Temperature & Humidity Sensor Module: KY-015 temperature and humidity sensor module, provides a low-latency serial interface to measure humidity and temperature.
